// Logisim project SequentialDivider.circ as structural Verilog: 1 circuit, main circuit Divider
module Divider (
  input  [3:0] Dividend,
  input  [3:0] Divisor,
  input  RESET,
  output [3:0] Quotient,
  output [3:0] Remainder,
  output DONE
);

  wire and_2_out, bitselector_1_out, nor_1_out, not_1_out, not_2_out, not_3_out, shift_register_1_p2;
  wire [2:0] counter_1_q;
  wire [7:0] bit_extender_1_out, multiplexer_1_out, register_1_q, shift_register_1_p19, subtractor_1_out;

  assign bit_extender_1_out = {{4{Dividend[3]}}, Dividend};  // Bit_Extender bit_extender_1
  Multiplexer #(.enable("false"), .width(8)) multiplexer_1 (
    .in0(subtractor_1_out), .in1(bit_extender_1_out), .out(multiplexer_1_out), .sel(RESET));
  // Shift_Register shift_register_1: pin names not known; wires that end beside it: RESET, shift_register_1_p2, 1'b0, Divisor[3], Divisor[2], Divisor[1], Divisor[0], 1'b0, 1'b0, 1'b0, 1'b0, shift_register_1_p19[7], shift_register_1_p19[6], shift_register_1_p19[5], shift_register_1_p19[4], shift_register_1_p19[3], shift_register_1_p19[2], shift_register_1_p19[1], shift_register_1_p19[0]
  Register register_1 (
    .D(multiplexer_1_out), .en(nor_1_out), .clk(shift_register_1_p2), .Q(register_1_q));  // open: clr
  Subtractor subtractor_1 (.a(register_1_q), .b(shift_register_1_p19), .out(subtractor_1_out));  // open: bin, bout
  Counter #(.max('h5), .ongoal("stay"), .width(3)) counter_1 (
    .clr(RESET), .clk(shift_register_1_p2), .Q(counter_1_q));  // open: load, up, count, D, carry
  BitSelector bitselector_1 (.in(multiplexer_1_out), .out(bitselector_1_out), .sel(3'b111));
  Clock clock_1 (.out(shift_register_1_p2));
  not not_1 (not_1_out, bitselector_1_out);
  not not_2 (not_2_out, DONE);
  nor nor_1 (nor_1_out, bitselector_1_out, DONE);
  // Shift_Register #(.length(4)) shift_register_2: pin names not known; wires that end beside it: RESET, not_2_out, shift_register_1_p2, not_1_out, 1'b0, 1'b0, 1'b0, 1'b0, Quotient[0], Quotient[1], Quotient[2], Quotient[3]
  Bit_Extender #(.out_width(4)) bit_extender_2 (.in(register_1_q), .out(Remainder));
  and and_1 (DONE, counter_1_q[0], and_2_out);
  and and_2 (and_2_out, not_3_out, counter_1_q[2]);
  not not_3 (not_3_out, counter_1_q[1]);

  // Notes on the sheet:
  //   Ye Yuan, 260921269
endmodule
