// Logisim project SequentialMultipler.circ as structural Verilog: 1 circuit, main circuit Multiplier
module Multiplier (
  input  [3:0] A,
  input  [3:0] B,
  input  RESET,
  output [7:0] PRODUCT,
  output DONE,
  output [7:0] out_6,
  output [7:0] out_7,
  output [7:0] out_8
);

  wire and_1_out, and_2_out, and_3_out, and_4_out, not_1_out, not_2_out, not_3_out, not_5_out, not_6_out,
       not_7_out, not_8_out, shift_register_1_p2, shift_register_1_p3, shift_register_2_p9;
  wire [2:0] counter_1_q;

  // Shift_Register shift_register_1: pin names not known; wires that end beside it: RESET, shift_register_1_p2, shift_register_1_p3, 1'b0, A[0], A[1], A[2], A[3], 1'b0, 1'b0, 1'b0, 1'b0, out_6[0], out_6[1], out_6[2], out_6[3], out_6[4], out_6[5], out_6[6], out_6[7]
  Adder adder_1 (.a(out_6), .b(out_8), .out(out_7));  // open: cin, cout
  Register register_1 (.D(out_7), .en(shift_register_2_p9), .clk(not_1_out), .Q(out_8), .clr(RESET));
  Clock clock_1 (.out(shift_register_1_p3));
  not not_1 (not_1_out, shift_register_1_p3);
  Counter #(.max('h7), .width(3)) counter_1 (
    .clr(RESET), .clk(shift_register_1_p3), .Q(counter_1_q));  // open: load, up, count, D, carry
  not not_2 (not_2_out, RESET);
  not not_3 (not_3_out, counter_1_q[0]);
  // Shift_Register #(.length(4)) shift_register_2: pin names not known; wires that end beside it: RESET, shift_register_1_p2, shift_register_1_p3, 1'b0, B[3], B[2], B[1], B[0], shift_register_2_p9
  not not_4 (shift_register_1_p2, and_1_out);
  and and_1 (and_1_out, not_5_out, and_2_out);
  not not_5 (not_5_out, counter_1_q[0]);
  and and_2 (and_2_out, not_6_out, not_7_out);
  not not_6 (not_6_out, counter_1_q[1]);
  not not_7 (not_7_out, counter_1_q[2]);
  not not_8 (not_8_out, counter_1_q[1]);
  and and_3 (and_3_out, not_3_out, counter_1_q[2]);
  and and_4 (and_4_out, and_3_out, not_8_out);
  Register register_2 (.D(out_8), .clk(DONE), .Q(PRODUCT), .clr(RESET));  // open: en
  Register #(.width(1)) register_3 (.D(not_2_out), .clk(and_4_out), .Q(DONE), .clr(RESET));  // open: en

  // Notes on the sheet:
  //   Ye Yuan, 260921269
endmodule
