// Logisim project led.circ as structural Verilog: 1 circuit, main circuit main
module main (
);

  wire and_1_out, and_2_out, and_3_out, and_4_out, and_5_out, and_6_out, and_7_out, and_8_out, and_9_out,
       and_10_out, and_11_out, and_12_out, and_13_out, and_14_out, and_15_out, and_16_out, and_17_out,
       and_18_out, and_19_out, and_20_out, and_21_out, and_22_out, and_23_out, and_24_out, and_25_out,
       and_26_out, and_27_out, clock_1_out, d_ff_1_q, d_ff_1_qn, d_ff_2_q, d_ff_2_qn, d_ff_3_q, d_ff_3_qn,
       d_ff_4_q, d_ff_4_qn, not_1_out, not_2_out, not_3_out, not_4_out, not_5_out, not_6_out, not_7_out,
       not_8_out, not_9_out, not_10_out, not_11_out, not_12_out, not_13_out, not_14_out, not_15_out,
       not_16_out, not_17_out, not_18_out, not_19_out, not_20_out, not_21_out, or_1_out, or_2_out, or_3_out,
       or_4_out, undriven, undriven_2, undriven_3, undriven_4, undriven_5;

  Clock clock_1 (.out(clock_1_out));
  D_Flip_Flop d_ff_1 (.D(d_ff_1_qn), .clk(d_ff_2_qn), .Q(d_ff_1_q), .Qn(d_ff_1_qn));  // open: preset, reset
  D_Flip_Flop d_ff_2 (.D(d_ff_2_qn), .clk(d_ff_3_qn), .Q(d_ff_2_q), .Qn(d_ff_2_qn));  // open: preset, reset
  D_Flip_Flop d_ff_3 (.D(d_ff_3_qn), .clk(d_ff_4_qn), .Q(d_ff_3_q), .Qn(d_ff_3_qn));  // open: preset, reset
  D_Flip_Flop d_ff_4 (.D(d_ff_4_qn), .clk(clock_1_out), .Q(d_ff_4_q), .Qn(d_ff_4_qn));  // open: preset, reset
  not not_1 (not_1_out, d_ff_1_q);
  not not_2 (not_2_out, d_ff_4_q);
  not not_3 (not_3_out, d_ff_4_q);
  not not_4 (not_4_out, d_ff_3_q);
  not not_5 (not_5_out, d_ff_3_q);
  not not_6 (not_6_out, d_ff_4_q);
  not not_7 (not_7_out, d_ff_4_q);
  not not_8 (not_8_out, d_ff_3_q);
  not not_9 (not_9_out, d_ff_3_q);
  and and_1 (and_1_out, not_1_out, d_ff_4_q);
  not not_10 (not_10_out, d_ff_2_q);
  and and_2 (and_2_out, not_2_out, d_ff_3_q);
  not not_11 (not_11_out, d_ff_2_q);
  and and_3 (and_3_out, d_ff_4_q, d_ff_3_q);
  not not_12 (not_12_out, d_ff_2_q);
  and and_4 (and_4_out, not_3_out, not_4_out);
  and and_5 (and_5_out, d_ff_4_q, not_5_out);
  and and_6 (and_6_out, not_6_out, d_ff_3_q);
  and and_7 (and_7_out, d_ff_4_q, d_ff_3_q);
  and and_8 (and_8_out, not_7_out, not_8_out);
  not not_13 (not_13_out, d_ff_2_q);
  and and_9 (and_9_out, d_ff_4_q, not_9_out);
  not not_14 (not_14_out, d_ff_2_q);
  and and_10 (and_10_out, and_1_out, not_10_out);
  and and_11 (and_11_out, and_10_out, not_15_out);
  not not_15 (not_15_out, d_ff_3_q);
  and and_12 (and_12_out, and_2_out, not_11_out);
  and and_13 (and_13_out, and_12_out, not_16_out);
  not not_16 (not_16_out, d_ff_1_q);
  and and_14 (and_14_out, and_3_out, not_12_out);
  and and_15 (and_15_out, and_14_out, not_17_out);
  not not_17 (not_17_out, d_ff_1_q);
  and and_16 (and_16_out, and_4_out, d_ff_2_q);
  and and_17 (and_17_out, and_16_out, not_18_out);
  not not_18 (not_18_out, d_ff_1_q);
  and and_18 (and_18_out, and_5_out, d_ff_2_q);
  and and_19 (and_19_out, and_18_out, not_19_out);
  not not_19 (not_19_out, d_ff_1_q);
  and and_20 (and_20_out, and_6_out, d_ff_2_q);
  and and_21 (and_21_out, and_20_out, not_20_out);
  not not_20 (not_20_out, d_ff_1_q);
  and and_22 (and_22_out, and_7_out, d_ff_2_q);
  and and_23 (and_23_out, and_22_out, not_21_out);
  not not_21 (not_21_out, d_ff_1_q);
  and and_24 (and_24_out, and_8_out, not_13_out);
  and and_25 (and_25_out, and_24_out, d_ff_1_q);
  and and_26 (and_26_out, and_9_out, not_14_out);
  and and_27 (and_27_out, and_26_out, d_ff_1_q);
  LED led_1 (.in(and_15_out));
  LED led_2 (.in(and_21_out));
  LED led_3 (.in(or_1_out));
  or or_1 (or_1_out, and_11_out, or_2_out);
  or or_2 (or_2_out, and_19_out, and_23_out);
  LED led_4 (.in(undriven_2));
  LED led_5 (.in(undriven));
  LED led_6 (.in(undriven_3));
  LED led_7 (.in(or_3_out));
  or or_3 (or_3_out, and_13_out, and_25_out);
  LED led_8 (.in(undriven_4));
  LED led_9 (.in(undriven_5));
  LED led_10 (.in(or_4_out));
  or or_4 (or_4_out, and_17_out, and_27_out);

  // Notes on the sheet:
  //   1
  //   0
  //   2
  //   3
  //   Ye Yuan, 260921269
  //   5
  //   4
  //   6
  //   7
  //   8
  //   9
endmodule
